// Digital circuit ALU.dig as structural Verilog
module ALU (
  input  [31:0] A,
  input  [31:0] B,
  input  [6:0] ALUOp,
  output zero,
  output [31:0] alu_out
);

  wire alu_ctrl_1_mode, not_1_out;
  wire [1:0] alu_ctrl_1_vecsize;
  wire [2:0] alu_ctrl_1_sel;
  wire [31:0] and_1_out, l_shifter_1_out, multiplexer_1_out, multiplexer_2_out, or_1_out, r_shifter_1_out,
       vector_adder_1_sum, xor_1_out;

  ALU_ctrl alu_ctrl_1 (.ctrl(ALUOp), .mode(alu_ctrl_1_mode), .vecSize(alu_ctrl_1_vecsize), .sel(alu_ctrl_1_sel));
  vector_adder vector_adder_1 (
    .A(A), .B(B), .vecSize(alu_ctrl_1_vecsize), .mode(alu_ctrl_1_mode), .sum(vector_adder_1_sum));
  Eq_Comp eq_comp_1 (.A(A), .B(B), .out(zero));
  R_Shifter r_shifter_1 (.data_in(A), .shift_in(B[4:0]), .out(r_shifter_1_out));
  L_Shifter l_shifter_1 (.data_in(A), .shift_in(B[4:0]), .out(l_shifter_1_out));
  assign and_1_out = A & B;  // And and_1, 32 bits wide
  assign or_1_out = A | B;  // Or or_1, 32 bits wide
  assign xor_1_out = A ^ B;  // XOr xor_1, 32 bits wide
  not not_1 (not_1_out, zero);
  Multiplexer #(.Bits(32)) multiplexer_1 (.sel(zero), .in_0({32{1'b0}}), .in_1(32'h1), .out(multiplexer_1_out));
  Multiplexer #(.Bits(32)) multiplexer_2 (.sel(not_1_out), .in_0({32{1'b0}}), .in_1(32'h1), .out(multiplexer_2_out));
  Multiplexer #(.Selector_Bits(3), .Bits(32)) multiplexer_3 (
    .sel(alu_ctrl_1_sel), .in_0(vector_adder_1_sum), .in_1(r_shifter_1_out), .in_2(multiplexer_1_out),
    .in_3(multiplexer_2_out), .in_4(l_shifter_1_out), .in_5(and_1_out), .in_6(or_1_out), .in_7(xor_1_out),
    .out(alu_out));
endmodule
