// Digital circuit ALU_ctrl.dig as structural Verilog
module ALU_ctrl (
  input  [6:0] ctrl,
  output mode,
  output [1:0] vecSize,
  output [2:0] sel
);


  assign mode = ctrl[5];
  assign sel = ctrl[2:0];
  assign vecSize = ctrl[4:3];
endmodule
