// Digital circuit Control.dig as structural Verilog
module Control (
  input  [31:0] instruction,
  input  clock,
  input  reset,
  output ALUsrc1,
  output [2:0] ALUOp,
  output ALUsrc,
  output branch,
  output MemRead,
  output MemWrite,
  output RegWrite,
  output MemToReg,
  output jump
);

  control #(.applicationType("GHDL")) u_control (
    .instruction(instruction), .clock(clock), .reset(reset), .ALUsrc1(ALUsrc1), .ALUOp(ALUOp),
    .ALUsrc(ALUsrc), .branch(branch), .MemRead(MemRead), .MemWrite(MemWrite), .RegWrite(RegWrite),
    .MemtoReg(MemToReg), .jump(jump));
  // Pins of 2 and 3 bits meet at ALUOp
endmodule

/* Code of control:
library IEEE;
use IEEE.STD_LOGIC_1164.ALL;
use IEEE.STD_LOGIC_UNSIGNED.ALL;

entity control is
    Port (
        instruction : in  STD_LOGIC_VECTOR(31 downto 0); -- 32 bits para instrução RV32I
        clock       : in  STD_LOGIC;
        reset       : in  STD_LOGIC;

        ALUsrc1     : out STD_LOGIC;
        ALUOp       : out STD_LOGIC_VECTOR(2 downto 0);  -- 3 bits para controle da ALU
        ALUsrc      : out STD_LOGIC;
        branch      : out STD_LOGIC;
        MemRead     : out STD_LOGIC;
        MemWrite    : out STD_LOGIC;
        RegWrite    : out STD_LOGIC;
        MemtoReg    : out STD_LOGIC;
        jump        : out STD_LOGIC
    );
end control;

architecture Behavioral of control is
begin
    process(clock, reset)
    begin
        if reset = '1' then
            ALUsrc1  <= '0';
            ALUOp    <= "000";
            ALUsrc   <= '0';
            branch   <= '0';
            MemRead  <= '0';
            MemWrite <= '0';
            RegWrite <= '0';
            MemtoReg <= '0';
            jump     <= '0';

        elsif rising_edge(clock) then
            case instruction(6 downto 0) is  -- opcode RISC-V (7 bits menos significativos)
                when "0110011" => -- R-type (add, sub, and, or, xor, sll, srl)
                    ALUsrc1  <= '0';
                    ALUOp    <= "010";
                    ALUsrc   <= '0';
                    branch   <= '0';
                    MemRead  <= '0';
                    MemWrite <= '0';
                    RegWrite <= '1';
                    MemtoReg <= '0';
                    jump     <= '0';

                when "0010011" => -- I-type (addi, andi, ori, xori, slli, srli)
                    ALUsrc1  <= '0';
                    ALUOp    <= "010";
                    ALUsrc   <= '1';
                    branch   <= '0';
                    MemRead  <= '0';
                    MemWrite <= '0';
                    RegWrite <= '1';
                    MemtoReg <= '0';
                    jump     <= '0';

                when "0000011" => -- lw
                    ALUsrc1  <= '0';
                    ALUOp    <= "000";
                    ALUsrc   <= '1';
                    branch   <= '0';
                    MemRead  <= '1';
                    MemWrite <= '0';
                    RegWrite <= '1';
                    MemtoReg <= '1';
                    jump     <= '0';

                when "0100011" => -- sw
                    ALUsrc1  <= '0';
                    ALUOp    <= "000";
                    ALUsrc   <= '1';
                    branch   <= '0';
                    MemRead  <= '0';
                    MemWrite <= '1';
                    RegWrite <= '0';
                    MemtoReg <= '0';
                    jump     <= '0';

                when "1100011" => -- branch (beq, bne)
                    ALUsrc1  <= '0';
                    ALUOp    <= "001";
                    ALUsrc   <= '0';
                    branch   <= '1';
                    MemRead  <= '0';
                    MemWrite <= '0';
                    RegWrite <= '0';
                    MemtoReg <= '0';
                    jump     <= '0';

                when "1101111" => -- jal
                    ALUsrc1  <= '0';
                    ALUOp    <= "000";
                    ALUsrc   <= '0';
                    branch   <= '0';
                    MemRead  <= '0';
                    MemWrite <= '0';
                    RegWrite <= '1';
                    MemtoReg <= '0';
                    jump     <= '1';

                when "1100111" => -- jalr
                    ALUsrc1  <= '0';
                    ALUOp    <= "000";
                    ALUsrc   <= '1';
                    branch   <= '0';
                    MemRead  <= '0';
                    MemWrite <= '0';
                    RegWrite <= '1';
                    MemtoReg <= '0';
                    jump     <= '1';

                when "0110111" => -- lui
                    ALUsrc1  <= '0';
                    ALUOp    <= "000";
                    ALUsrc   <= '1';
                    branch   <= '0';
                    MemRead  <= '0';
                    MemWrite <= '0';
                    RegWrite <= '1';
                    MemtoReg <= '0';
                    jump     <= '0';

                when "0010111" => -- auipc
                    ALUsrc1  <= '1';
                    ALUOp    <= "000";
                    ALUsrc   <= '1';
                    branch   <= '0';
                    MemRead  <= '0';
                    MemWrite <= '0';
                    RegWrite <= '1';
                    MemtoReg <= '0';
                    jump     <= '0';

                when others =>
                    ALUsrc1  <= '0';
                    ALUOp    <= "000";
                    ALUsrc   <= '0';
                    branch   <= '0';
                    MemRead  <= '0';
                    MemWrite <= '0';
                    RegWrite <= '0';
                    MemtoReg <= '0';
                    jump     <= '0';
            end case;
        end if;
    end process;

end Behavioral;
*/
