// Digital circuit EX-MEM_stage.dig as structural Verilog
module EX_MEM_stage (
  input  clk,
  input  reset,
  input  zero,
  input  branch,
  input  mem_rd,
  input  mem_wr,
  input  reg_wr,
  input  mem_reg,
  input  jump_in,
  input  [31:0] rs2,
  input  [31:0] ALU_res,
  input  [31:0] pc_4,
  input  [31:0] pc_imm,
  input  [31:0] imm,
  input  [4:0] rd,
  output zero_out,
  output branch_out,
  output mem_rdout,
  output mem_wrout,
  output reg_wrout,
  output mem_regout,
  output [31:0] ALU_resout,
  output [31:0] rs2_out,
  output [31:0] pc_4out
);

  Ex_Mem #(.applicationType("GHDL")) u_Ex_Mem (
    .clock_i(clk), .reset_i(reset), .zero_in(zero), .branch_in(branch), .mem_read_in(mem_rd),
    .mem_write_in(mem_wr), .reg_write_in(reg_wr), .mem_to_reg_in(mem_reg), .jump_in(jump_in),
    .ALU_res_in(ALU_res), .rs2_in(rs2), .pc_mais_4_in(pc_4), .pc_imm_in(pc_imm), .imm_in(imm), .rd_in(rd),
    .zero_out(zero_out), .branch_out(branch_out), .mem_read_out(mem_rdout), .mem_write_out(mem_wrout),
    .reg_write_out(reg_wrout), .mem_to_reg_out(mem_regout), .ALU_res_out(ALU_resout), .rs2_out(rs2_out),
    .pc_mais_4_out(pc_4out));
endmodule

/* Code of Ex_Mem:
library IEEE;
use IEEE.STD_LOGIC_1164.ALL;
use IEEE.NUMERIC_STD.ALL;

entity Ex_Mem is
    Port ( 
        clock_i         : in  STD_LOGIC;
        reset_i         : in  STD_LOGIC;
        
        zero_in         : in  STD_LOGIC;
        branch_in       : in  STD_LOGIC;
        mem_read_in     : in  STD_LOGIC;
        mem_write_in    : in  STD_LOGIC;
        reg_write_in    : in  STD_LOGIC;
        mem_to_reg_in   : in  STD_LOGIC;
        jump_in         : in  STD_LOGIC;
        ALU_res_in      : in  STD_LOGIC_VECTOR(31 downto 0);
        rs2_in          : in  STD_LOGIC_VECTOR(31 downto 0);
        pc_mais_4_in    : in  STD_LOGIC_VECTOR(31 downto 0);
        pc_imm_in       : in  STD_LOGIC_VECTOR(31 downto 0);
        imm_in          : in  STD_LOGIC_VECTOR(31 downto 0);
        rd_in           : in  STD_LOGIC_VECTOR(4 downto 0);

        zero_out        : out STD_LOGIC;
        branch_out      : out STD_LOGIC;
        mem_read_out    : out STD_LOGIC;
        mem_write_out   : out STD_LOGIC;
        reg_write_out   : out STD_LOGIC;
        mem_to_reg_out  : out STD_LOGIC;
        ALU_res_out     : out STD_LOGIC_VECTOR(31 downto 0);
        rs2_out         : out STD_LOGIC_VECTOR(31 downto 0);
        pc_mais_4_out   : out STD_LOGIC_VECTOR(31 downto 0)
    );
end Ex_Mem;

architecture Behavioral of Ex_Mem is
begin
    process(clock_i, reset_i)
    begin
        if reset_i = '1' then
            zero_out        <= '0';
            branch_out      <= '0';
            mem_read_out    <= '0';
            mem_write_out   <= '0';
            reg_write_out   <= '0';
            mem_to_reg_out  <= '0';
            ALU_res_out     <= (others => '0');
            rs2_out         <= (others => '0');
            pc_mais_4_out   <= (others => '0');
        elsif rising_edge(clock_i) then
            zero_out        <= zero_in;
            branch_out      <= branch_in;
            mem_read_out    <= mem_read_in;
            mem_write_out   <= mem_write_in;
            reg_write_out   <= reg_write_in;
            mem_to_reg_out  <= mem_to_reg_in;
            ALU_res_out     <= ALU_res_in;
            rs2_out         <= rs2_in;
            pc_mais_4_out   <= pc_mais_4_in;
        end if;
    end process;
end Behavioral;
*/
