// Digital circuit Eq_Comp.dig as structural Verilog
module Eq_Comp (
  input  [31:0] A,
  input  [31:0] B,
  output out
);

  Eq_Comp #(.applicationType("GHDL")) u_Eq_Comp (.A(A), .B(B), .EQ(out));
endmodule

/* Code of Eq_Comp:
library IEEE;
use IEEE.STD_LOGIC_1164.ALL;

entity Eq_Comp is
    port (
        A : in  STD_LOGIC_VECTOR(31 downto 0);
        B : in  STD_LOGIC_VECTOR(31 downto 0);
        EQ       : out STD_LOGIC
    );
end entity Eq_Comp;

architecture Behavioral of Eq_Comp is
begin
    EQ <= '1' when A = B else '0';

end architecture Behavioral;
*/
