// Digital circuit ID-EX_stage.dig as structural Verilog
module ID_EX_stage (
  input  clk,
  input  off,
  input  mem_reg,
  input  reg_wr,
  input  mem_wr,
  input  mem_rd,
  input  ALUsrc,
  input  branch,
  input  [2:0] ALUOP,
  input  [31:0] rs1,
  input  [31:0] rs2,
  input  [31:0] imm_gen,
  input  [31:0] pc_4,
  input  [4:0] rd,
  output mem_reg_out,
  output reg_wrout,
  output mem_wrout,
  output mem_rdout,
  output ALUsrc_out,
  output branch_out,
  output [2:0] ALUOP_out,
  output [31:0] rs1_out,
  output [31:0] rs2_out,
  output [31:0] imm_gen_out,
  output [31:0] pc_4out,
  output [4:0] rd_out
);

  ID_EX #(.applicationType("GHDL")) u_ID_EX (
    .clk_i(clk), .turn_off_i(off), .Mem_to_Reg_in(mem_reg), .Reg_Write_in(reg_wr), .Mem_Write_in(mem_wr),
    .Mem_Read_in(mem_rd), .ALUsrc_in(ALUsrc), .branch_in(branch), .ALUOP_in(ALUOP), .rs1_in(rs1),
    .rs2_in(rs2), .imm_gen_in(imm_gen), .pc_mais_4_in(pc_4), .rd_in(rd), .Mem_to_Reg_out(mem_reg_out),
    .Reg_Write_out(reg_wrout), .Mem_Write_out(mem_wrout), .Mem_Read_out(mem_rdout), .ALUsrc_out(ALUsrc_out),
    .branch_out(branch_out), .ALUOP_out(ALUOP_out), .rs1_out(rs1_out), .rs2_out(rs2_out),
    .imm_gen_out(imm_gen_out), .pc_mais_4_out(pc_4out), .rd_out(rd_out));
endmodule

/* Code of ID_EX:
library IEEE;
use IEEE.STD_LOGIC_1164.ALL;
use IEEE.NUMERIC_STD.ALL;

entity ID_EX is
    Port ( 
        clk_i           : in  STD_LOGIC;
        turn_off_i      : in  STD_LOGIC;
        Mem_to_Reg_in   : in  STD_LOGIC;
        Reg_Write_in    : in  STD_LOGIC;
        Mem_Write_in    : in  STD_LOGIC;
        Mem_Read_in     : in  STD_LOGIC;
        ALUsrc_in       : in  STD_LOGIC;
        branch_in       : in  STD_LOGIC;
        ALUOP_in        : in  STD_LOGIC_VECTOR(2 downto 0);
        rs1_in          : in  STD_LOGIC_VECTOR(31 downto 0);
        rs2_in          : in  STD_LOGIC_VECTOR(31 downto 0);
        imm_gen_in      : in  STD_LOGIC_VECTOR(31 downto 0);
        pc_mais_4_in    : in  STD_LOGIC_VECTOR(31 downto 0);
        rd_in           : in  STD_LOGIC_VECTOR(4 downto 0);
        Mem_to_Reg_out  : out STD_LOGIC;
        Reg_Write_out   : out STD_LOGIC;
        Mem_Write_out   : out STD_LOGIC;
        Mem_Read_out    : out STD_LOGIC;
        ALUsrc_out      : out STD_LOGIC;
        branch_out      : out STD_LOGIC;
        ALUOP_out       : out STD_LOGIC_VECTOR(2 downto 0);
        rs1_out         : out STD_LOGIC_VECTOR(31 downto 0);
        rs2_out         : out STD_LOGIC_VECTOR(31 downto 0);
        imm_gen_out     : out STD_LOGIC_VECTOR(31 downto 0);
        pc_mais_4_out   : out STD_LOGIC_VECTOR(31 downto 0);
        rd_out          : out STD_LOGIC_VECTOR(4 downto 0)
    );
end ID_EX;

architecture Behavioral of ID_EX is
begin
    process(clk_i)
    begin
        if rising_edge(clk_i) then
            if turn_off_i = '0' then
                Mem_to_Reg_out  <= Mem_to_Reg_in;
                Reg_Write_out   <= Reg_Write_in;
                Mem_Write_out   <= Mem_Write_in;
                Mem_Read_out    <= Mem_Read_in;
                ALUsrc_out      <= ALUsrc_in;
                branch_out      <= branch_in;
                ALUOP_out       <= ALUOP_in;
                rs1_out         <= rs1_in;
                rs2_out         <= rs2_in;
                imm_gen_out     <= imm_gen_in;
                pc_mais_4_out   <= pc_mais_4_in;
                rd_out          <= rd_in;
            end if;
        end if;
    end process;
end Behavioral;
*/
