// Digital circuit L_Shifter.dig as structural Verilog
module L_Shifter (
  input  [31:0] data_in,
  input  [4:0] shift_in,
  output [31:0] out
);

  L_Shifter #(.applicationType("GHDL")) u_L_Shifter (.data_in_i(data_in), .shift_amount_i(shift_in), .data_out_o(out));
endmodule

/* Code of L_Shifter:
library IEEE;
use IEEE.STD_LOGIC_1164.ALL;
use IEEE.NUMERIC_STD.ALL;

entity L_Shifter is
    Port ( 
        data_in_i      : in  STD_LOGIC_VECTOR (31 downto 0);
        shift_amount_i : in  STD_LOGIC_VECTOR (4 downto 0); -- 5 bits para deslocar até 31 posições
        data_out_o     : out STD_LOGIC_VECTOR (31 downto 0)
    );
end L_Shifter;

architecture Behavioral of L_Shifter is
begin
    data_out_o <= std_logic_vector(shift_left(unsigned(data_in_i), to_integer(unsigned(shift_amount_i))));
end Behavioral;
*/
