// Digital circuit R_Shifter.dig as structural Verilog
module R_Shifter (
  input  [31:0] data_in,
  input  [4:0] shift_in,
  output [31:0] out
);

  R_Shifter #(.applicationType("GHDL")) u_R_Shifter (.data_in_i(data_in), .shift_amount_i(shift_in), .data_out_o(out));
endmodule

/* Code of R_Shifter:
library IEEE;
use IEEE.STD_LOGIC_1164.ALL;
use IEEE.NUMERIC_STD.ALL;

entity R_Shifter is
    Port ( 
        data_in_i      : in  STD_LOGIC_VECTOR (31 downto 0);
        shift_amount_i : in  STD_LOGIC_VECTOR (4 downto 0);
        data_out_o     : out STD_LOGIC_VECTOR (31 downto 0)
    );
end R_Shifter;

architecture Behavioral of R_Shifter is
begin
    data_out_o <= std_logic_vector(shift_right(unsigned(data_in_i), to_integer(unsigned(shift_amount_i))));
end Behavioral;
*/
