// Digital circuit Registers.dig as structural Verilog
module Registers (
  input  clock,
  input  reset,
  input  register_write,
  input  [4:0] read_register_1,
  input  [4:0] read_register_2,
  input  [4:0] write_register,
  input  [31:0] write_data,
  output [31:0] read_data_1,
  output [31:0] read_data_2
);

  register_file #(.applicationType("GHDL")) u_register_file (
    .clk(clock), .reset(reset), .reg_write(register_write), .read_reg1(read_register_1),
    .read_reg2(read_register_2), .write_reg(write_register), .write_data(write_data),
    .read_data1(read_data_1), .read_data2(read_data_2));
endmodule

/* Code of register_file:
library IEEE;
use IEEE.STD_LOGIC_1164.ALL;
use IEEE.NUMERIC_STD.ALL;

entity register_file is
    port (
        clk, reset : in std_logic;
        reg_write : in std_logic;
        read_reg1, read_reg2, write_reg : in std_logic_vector(4 downto 0);
        write_data : in std_logic_vector(31 downto 0);
        read_data1, read_data2 : out std_logic_vector(31 downto 0)
    );
end entity;

architecture behavioral of register_file is
    -- Array de 32 registradores de 32 bits
    type reg_array is array (0 to 31) of std_logic_vector(31 downto 0);
    signal registers : reg_array;
    
begin
    process(clk, reset)
    begin
        if reset = '1' then
            -- Reset assíncrono: inicializa todos os registradores
            for i in 0 to 31 loop
                registers(i) <= (others => '0');
            end loop;
            
        elsif rising_edge(clk) then
            -- Escrita síncrona no estágio WB
            if reg_write = '1' then
                -- Não permite escrita no registrador x0
                if write_reg /= "00000" then
                    registers(to_integer(unsigned(write_reg))) <= write_data;
                end if;
            end if;
        end if;
    end process;
    
    -- Leitura assíncrona (combinacional) no estágio ID
    read_data1 <= (others => '0') when read_reg1 = "00000" else 
                  registers(to_integer(unsigned(read_reg1)));
    
    read_data2 <= (others => '0') when read_reg2 = "00000" else 
                  registers(to_integer(unsigned(read_reg2)));
    
end architecture;
*/
