// Digital circuit add_Sum.dig as structural Verilog
module add_Sum (
  input  [31:0] Data_1,
  input  [31:0] Data_2,
  output [31:0] Result
);

  add_sum #(.applicationType("GHDL")) u_add_sum (.data_1(Data_1), .data_2(Data_2), .result(Result));
endmodule

/* Code of add_sum:
library IEEE;
use IEEE.STD_LOGIC_1164.ALL;
use IEEE.NUMERIC_STD.ALL;

entity add_sum is
    Port (
        data_1  : in  STD_LOGIC_VECTOR(31 downto 0);
        data_2  : in  STD_LOGIC_VECTOR(31 downto 0);
        result : out STD_LOGIC_VECTOR(31 downto 0)
    );
end add_sum;

architecture Behavioral of add_sum is
begin
    process(data_1, data_2)
    begin
       result <= std_logic_vector(signed(data_1) + signed(data_2));
    end process;
end Behavioral;
*/
