// Digital circuit assync_Input.dig as structural Verilog
module assync_Input (
  input  [31:0] sync_address,
  input  [31:0] sync_data,
  input  [31:0] assync_address,
  input  [31:0] assync_data,
  input  assync,
  output [31:0] address_out,
  output [31:0] data_output
);

  assync_input #(.applicationType("GHDL")) u_assync_input (
    .sync_address(sync_address), .sync_data(sync_data), .assync_address(assync_address),
    .assync_data(assync_data), .assync(assync), .address_out(address_out), .data_output(data_output));
endmodule

/* Code of assync_input:
library IEEE;
use IEEE.STD_LOGIC_1164.ALL;

entity assync_input is
    Port (
        sync_address     : in  STD_LOGIC_VECTOR(31 downto 0);
        sync_data        : in  STD_LOGIC_VECTOR(31 downto 0);
        assync_address   : in  STD_LOGIC_VECTOR(31 downto 0);
        assync_data      : in  STD_LOGIC_VECTOR(31 downto 0);
        assync           : in  STD_LOGIC;

        address_out      : out STD_LOGIC_VECTOR(31 downto 0);
        data_output      : out STD_LOGIC_VECTOR(31 downto 0)
    );
end assync_input;

architecture Behavioral of assync_input is
begin
    process(sync_address, sync_data, assync_address, assync_data, assync)
    begin
        if assync = '1' then
            address_out <= assync_address;
            data_output <= assync_data;
        else
            address_out <= sync_address;
            data_output <= sync_data;
        end if;
    end process;
end Behavioral;
*/
