// Digital circuit cpu.dig as structural Verilog
module cpu (
  input  stall,
  input  [31:0] instruction_in,
  input  [31:0] pc_in,
  input  reset,
  input  clock,
  input  turn_off
);

  wire alu_1_zero, control_1_p4, control_1_p5, control_1_p7, control_1_p8, control_1_p9, control_1_p10,
       control_1_p11, ex_mem_stage_1_mem_regout, ex_mem_stage_1_reg_wrout, hazard_unit_1_stall,
       id_ex_stage_1_p15, id_ex_stage_1_p16, id_ex_stage_1_p17, id_ex_stage_1_p18, id_ex_stage_1_p19,
       id_ex_stage_1_p20, mem_wb_stage_1_mem_to_reg_ou, mem_wb_stage_1_reg_write_out;
  wire [1:0] forward_unit_1_forwarda, forward_unit_1_forwardb;
  wire [2:0] id_ex_stage_1_p21;
  wire [4:0] id_ex_stage_1_p26, if_id_stage_1_rd, if_id_stage_1_rs1, if_id_stage_1_rs1_2, if_id_stage_1_rs2,
       if_id_stage_1_rs2_2, mem_wb_stage_1_rd_out;
  wire [31:0] add_sum_1_result, alu_1_alu_out, ex_mem_stage_1_alu_resout, ex_mem_stage_1_pc_4out,
       id_ex_stage_1_p22, id_ex_stage_1_p23, id_ex_stage_1_p24, id_ex_stage_1_p25,
       if_id_stage_1_intruction_out, if_id_stage_1_pc__plus_4_out, imm_gen_1_immediate,
       mem_wb_stage_1_alu_res_out, mem_wb_stage_1_mem_data_out, multiplexer_1_out, multiplexer_2_out,
       multiplexer_3_out, multiplexer_4_out, registers_1_read_data_1, registers_1_read_data_2, write_data;

  IF_ID_stage if_id_stage_1 (
    .clock(clock), .turn_off(turn_off), .stall(hazard_unit_1_stall), .instruction_in(instruction_in),
    .pc_in(pc_in), .reset(reset), .intruction_out(if_id_stage_1_intruction_out),
    .pc__plus_4_out(if_id_stage_1_pc__plus_4_out), .rs2(if_id_stage_1_rs2), .rs1(if_id_stage_1_rs1),
    .rd(if_id_stage_1_rd), .rs2_2(if_id_stage_1_rs2_2), .rs1_2(if_id_stage_1_rs1_2));  // open: pc_out
  imm_Gen imm_gen_1 (.instruction(if_id_stage_1_intruction_out), .immediate(imm_gen_1_immediate));
  // Control control_1: pin names not known; wires that end beside it: if_id_stage_1_intruction_out, clock, reset, control_1_p4, control_1_p5, control_1_p4, control_1_p7, control_1_p8, control_1_p9, control_1_p10, control_1_p11
  Registers registers_1 (
    .clock(clock), .reset(reset), .register_write(mem_wb_stage_1_reg_write_out),
    .read_register_1(if_id_stage_1_rs2), .read_register_2(if_id_stage_1_rs1),
    .write_register(mem_wb_stage_1_rd_out), .write_data(write_data), .read_data_1(registers_1_read_data_1),
    .read_data_2(registers_1_read_data_2));
  // ID_EX_stage id_ex_stage_1: pin names not known; wires that end beside it: clock, turn_off, control_1_p11, control_1_p10, control_1_p9, control_1_p8, control_1_p4, control_1_p7, control_1_p5, registers_1_read_data_1, registers_1_read_data_2, imm_gen_1_immediate, if_id_stage_1_pc__plus_4_out, if_id_stage_1_rd, id_ex_stage_1_p15, id_ex_stage_1_p16, id_ex_stage_1_p17, id_ex_stage_1_p18, id_ex_stage_1_p19, id_ex_stage_1_p20, id_ex_stage_1_p21, id_ex_stage_1_p22, id_ex_stage_1_p23, id_ex_stage_1_p24, id_ex_stage_1_p25, id_ex_stage_1_p26
  hazard_unit hazard_unit_1 (
    .clock(clock), .IdRs1(if_id_stage_1_rs1_2), .IdRs2(if_id_stage_1_rs2_2), .ExRd(id_ex_stage_1_p26),
    .ExMemRd(id_ex_stage_1_p18), .stall(hazard_unit_1_stall));
  forward_unit forward_unit_1 (
    .clock(clock), .wbRegWrite(mem_wb_stage_1_reg_write_out), .MemRegWrite(ex_mem_stage_1_mem_regout),
    .ExRs1(id_ex_stage_1_p22[4:0]), .ExRs2(id_ex_stage_1_p23[4:0]), .MemRd(id_ex_stage_1_p26),
    .wbRD(mem_wb_stage_1_rd_out), .ForwardA(forward_unit_1_forwarda), .ForwardB(forward_unit_1_forwardb));
  Multiplexer #(.Bits(32)) multiplexer_1 (
    .sel(id_ex_stage_1_p19), .in_0(id_ex_stage_1_p24), .in_1(id_ex_stage_1_p25), .out(multiplexer_1_out));
  Multiplexer #(.Bits(32)) multiplexer_2 (
    .sel(id_ex_stage_1_p19), .in_0(id_ex_stage_1_p23), .in_1(id_ex_stage_1_p24), .out(multiplexer_2_out));
  add_Sum add_sum_1 (.Data_1(id_ex_stage_1_p25), .Data_2(id_ex_stage_1_p24), .Result(add_sum_1_result));
  Multiplexer #(.Selector_Bits(2), .Bits(32)) multiplexer_3 (
    .sel(forward_unit_1_forwarda), .in_0({32{1'b0}}), .in_1({32{1'b0}}), .in_2(multiplexer_1_out),
    .in_3({32{1'b0}}), .out(multiplexer_3_out));
  Multiplexer #(.Selector_Bits(2), .Bits(32)) multiplexer_4 (
    .sel(forward_unit_1_forwardb), .in_0({32{1'b0}}), .in_1(multiplexer_2_out), .in_2({32{1'b0}}),
    .in_3({32{1'b0}}), .out(multiplexer_4_out));
  ALU alu_1 (
    .A(multiplexer_3_out), .B(multiplexer_4_out), .ALUOp({4'b0000, id_ex_stage_1_p21}), .zero(alu_1_zero),
    .alu_out(alu_1_alu_out));
  EX_MEM_stage ex_mem_stage_1 (
    .clk(clock), .reset(reset), .zero(alu_1_zero), .branch(id_ex_stage_1_p20), .mem_rd(id_ex_stage_1_p18),
    .mem_wr(id_ex_stage_1_p17), .reg_wr(id_ex_stage_1_p16), .mem_reg(id_ex_stage_1_p15),
    .jump_in(id_ex_stage_1_p19), .rs2(id_ex_stage_1_p23), .ALU_res(alu_1_alu_out), .pc_4(id_ex_stage_1_p25),
    .pc_imm(add_sum_1_result), .imm(id_ex_stage_1_p24), .rd(id_ex_stage_1_p26),
    .reg_wrout(ex_mem_stage_1_reg_wrout), .mem_regout(ex_mem_stage_1_mem_regout),
    .ALU_resout(ex_mem_stage_1_alu_resout), .pc_4out(ex_mem_stage_1_pc_4out));  // open: zero_out, branch_out, mem_rdout, mem_wrout, rs2_out
  MEM_WB_stage mem_wb_stage_1 (
    .clock(clock), .reset(reset), .turn_off(turn_off), .reg_write_in(ex_mem_stage_1_reg_wrout),
    .mem_to_reg_in(ex_mem_stage_1_mem_regout), .mem_data_in(ex_mem_stage_1_alu_resout),
    .ALU_res_in(alu_1_alu_out), .rd_in(id_ex_stage_1_p26), .pc_mais_4_in(ex_mem_stage_1_pc_4out),
    .imm_in(add_sum_1_result), .reg_write_out(mem_wb_stage_1_reg_write_out),
    .mem_to_reg_ou(mem_wb_stage_1_mem_to_reg_ou), .mem_data_out(mem_wb_stage_1_mem_data_out),
    .ALU_res_out(mem_wb_stage_1_alu_res_out), .rd_out(mem_wb_stage_1_rd_out));  // open: pc_mais_4_out, imm_out
  Multiplexer #(.Bits(32)) multiplexer_5 (
    .sel(mem_wb_stage_1_mem_to_reg_ou), .in_0(mem_wb_stage_1_mem_data_out),
    .in_1(mem_wb_stage_1_alu_res_out), .out(write_data));
endmodule
