// Digital circuit forward_unit.dig as structural Verilog
module forward_unit (
  input  clock,
  input  wbRegWrite,
  input  MemRegWrite,
  input  [4:0] ExRs1,
  input  [4:0] ExRs2,
  input  [4:0] MemRd,
  input  [4:0] wbRD,
  output [1:0] ForwardA,
  output [1:0] ForwardB
);

  forward_unit #(.applicationType("GHDL")) u_forward_unit (
    .clock(clock), .WbRegWrite(wbRegWrite), .MemRegWrite(MemRegWrite), .ExRs1(ExRs1), .ExRs2(ExRs2),
    .MemRd(MemRd), .WbRd(wbRD), .ForwardA(ForwardA), .ForwardB(ForwardB));
endmodule

/* Code of forward_unit:
library IEEE;
use IEEE.STD_LOGIC_1164.ALL;
use IEEE.STD_LOGIC_UNSIGNED.ALL;

entity forward_unit is
    Port (
        clock         : in  STD_LOGIC;
        WbRegWrite    : in  STD_LOGIC;
        MemRegWrite   : in  STD_LOGIC;
        ExRs1         : in  STD_LOGIC_VECTOR(4 downto 0);
        ExRs2         : in  STD_LOGIC_VECTOR(4 downto 0);
        MemRd         : in  STD_LOGIC_VECTOR(4 downto 0);
        WbRd          : in  STD_LOGIC_VECTOR(4 downto 0);
        ForwardA      : out STD_LOGIC_VECTOR(1 downto 0);
        ForwardB      : out STD_LOGIC_VECTOR(1 downto 0)
    );
end forward_unit;

architecture Behavioral of forward_unit is
begin
    process(clock)
    begin
        if rising_edge(clock) then
            -- Default (sem forwarding)
            ForwardA <= "00";
            ForwardB <= "00";

            -- Encaminhamento para ForwardA
            if (MemRegWrite = '1' and MemRd /= "00000" and MemRd = ExRs1) then
                ForwardA <= "10";
            elsif (WbRegWrite = '1' and WbRd /= "00000" and WbRd = ExRs1) then
                ForwardA <= "01";
            end if;

            -- Encaminhamento para ForwardB
            if (MemRegWrite = '1' and MemRd /= "00000" and MemRd = ExRs2) then
                ForwardB <= "10";
            elsif (WbRegWrite = '1' and WbRd /= "00000" and WbRd = ExRs2) then
                ForwardB <= "01";
            end if;
        end if;
    end process;
end Behavioral;
*/
