// Digital circuit hazard_unit.dig as structural Verilog
module hazard_unit (
  input  clock,
  input  [4:0] IdRs1,
  input  [4:0] IdRs2,
  input  [4:0] ExRd,
  input  ExMemRd,
  output stall
);

  hazard_unit #(.applicationType("GHDL")) u_hazard_unit (
    .clock(clock), .IdRs1(IdRs1), .IdRs2(IdRs2), .ExRd(ExRd), .ExMemRd(ExMemRd), .stall(stall));
endmodule

/* Code of hazard_unit:
library IEEE;
use IEEE.STD_LOGIC_1164.ALL;
use IEEE.STD_LOGIC_UNSIGNED.ALL;

entity hazard_unit is
    Port (
        clock     : in  STD_LOGIC;
        IdRs1     : in  STD_LOGIC_VECTOR(4 downto 0);
        IdRs2     : in  STD_LOGIC_VECTOR(4 downto 0);
        ExRd      : in  STD_LOGIC_VECTOR(4 downto 0);
        ExMemRd   : in  STD_LOGIC; -- MemRead da instrução em EX
        stall     : out STD_LOGIC
    );
end hazard_unit;

architecture Behavioral of hazard_unit is
begin
    process(clock)
    begin
        if rising_edge(clock) then
            if (ExMemRd = '1') and (
                (ExRd /= "00000") and 
                ((ExRd = IdRs1) or (ExRd = IdRs2))
            ) then
                stall <= '1'; -- hazard detectado
            else
                stall <= '0'; -- sem hazard
            end if;
        end if;
    end process;
end Behavioral;
*/
