// Digital circuit imm_Gen.dig as structural Verilog
module imm_Gen (
  input  [31:0] instruction,
  output [31:0] immediate
);

  imm_gen #(.applicationType("GHDL")) u_imm_gen (.instruction(instruction), .immediate(immediate));
endmodule

/* Code of imm_gen:
library ieee;
use ieee.std_logic_1164.all;
use ieee.numeric_std.all;

entity imm_gen is
    port (
        instruction : in  std_logic_vector(31 downto 0);
        immediate   : out std_logic_vector(31 downto 0)
    );
end entity imm_gen;

architecture fluxo_dados of imm_gen is
    signal opc_s : std_logic_vector(6 downto 0);
begin

    process(instruction, opc_s)
        variable valor_temp : std_logic_vector(31 downto 0);
    begin
        opc_s <= instruction(6 downto 0);

        case opc_s is
            when "0000011" | "0010011" | "1100111" =>
                valor_temp := (others => instruction(31));
                valor_temp(11 downto 0) := instruction(31 downto 20);
                immediate <= valor_temp;

            when "0100011" =>
                valor_temp := (others => instruction(31));
                valor_temp(11 downto 5) := instruction(31 downto 25);
                valor_temp(4 downto 0)  := instruction(11 downto 7);
                immediate <= valor_temp;

            when "1100011" =>
                valor_temp := (others => instruction(31));
                valor_temp(12)         := instruction(31);
                valor_temp(11)         := instruction(7);
                valor_temp(10 downto 5) := instruction(30 downto 25);
                valor_temp(4 downto 1) := instruction(11 downto 8);
                valor_temp(0)          := '0';
                immediate <= valor_temp;

            when "0110111" | "0010111" =>
                valor_temp := instruction(31 downto 12) & (11 downto 0 => '0');
                immediate <= valor_temp;

            when "1101111" =>
                valor_temp := (others => instruction(31));
                valor_temp(20)         := instruction(31);
                valor_temp(19 downto 12) := instruction(19 downto 12);
                valor_temp(11)         := instruction(20);
                valor_temp(10 downto 1) := instruction(30 downto 21);
                valor_temp(0)          := '0';
                immediate <= valor_temp;

            when "1010100" | "1010101" | "1010110" =>
                valor_temp := (others => instruction(31));
                valor_temp(11 downto 0) := instruction(31 downto 20);
                immediate <= valor_temp;

            when "1011000" | "1011001" | "1011010" =>
                valor_temp := instruction(31 downto 12) & (11 downto 0 => '0');
                immediate <= valor_temp;

            when "1010000" | "1010001" | "1010010" =>
                immediate <= (others => '0');

            when others =>
                immediate <= (others => '0');
        end case;
    end process;

end architecture fluxo_dados;
*/
