// Digital circuit instruct_comp.dig as structural Verilog
module instruct_comp (
  input  [6:0] op_code,
  input  [6:0] \const ,
  output output_1
);

  instruct_comp #(.applicationType("GHDL")) u_instruct_comp (.op_code(op_code), .\const (\const ), .output_1(output_1));
endmodule

/* Code of instruct_comp:
library IEEE;
use IEEE.STD_LOGIC_1164.ALL;

entity instruct_comp is
    port (
        op_code    : in  STD_LOGIC_VECTOR(6 downto 0);
        const : in  STD_LOGIC_VECTOR(6 downto 0);
        output_1  : out STD_LOGIC
    );
end entity instruct_comp;

architecture Behavioral of instruct_comp is
begin
    output_1 <= '1' when (op_code = const) else '0';
end architecture Behavioral;
*/
